// Digital circuit BAD_APPLE.dig as structural Verilog
module BAD_APPLE (
  input  clk,
  input  in_2,
  input  in_3
);

  wire not_1_out, s1_single_cycle_1_mem_we, u_video_to_vram;
  wire [3:0] counter_1_out;
  wire [7:0] s1_single_cycle_1_inst_addr;
  wire [8:0] u_video_vram_addr;
  wire [23:0] s1_single_cycle_1_data_addr;
  wire [29:8] s1_single_cycle_1_inst_addr_2;
  wire [29:24] s1_single_cycle_1_data_addr_2;
  wire [31:0] rom_1_d, rom_2_d, s1_single_cycle_1_data_out;

  Counter #(.Bits(4)) counter_1 (.en(1'b1), .C(clk), .clr(1'b0), .out(counter_1_out));  // open: ovf
  ROM #(.bigEndian("true"), .AddrBits(8), .Bits(32)) rom_1 (.A(s1_single_cycle_1_inst_addr), .sel(1'b1), .D(rom_1_d));
  ROM #(.bigEndian("true"), .AddrBits(24), .Bits(32)) rom_2 (.A(s1_single_cycle_1_data_addr), .sel(1'b1), .D(rom_2_d));
  s1_single_cycle s1_single_cycle_1 (
    .inst_in(rom_1_d), .clk(counter_1_out[3]), .data_in(rom_2_d), .clk_en(in_2), .rst(in_3),
    .inst_addr({s1_single_cycle_1_inst_addr_2, s1_single_cycle_1_inst_addr}),
    .data_addr({s1_single_cycle_1_data_addr_2, s1_single_cycle_1_data_addr}),
    .data_out(s1_single_cycle_1_data_out), .mem_we(s1_single_cycle_1_mem_we));  // open: mask, mem_lock
  video #(.applicationType("IVERILOG"), .iverilogOptions("-g2012")) u_video (
    .address({s1_single_cycle_1_data_addr_2, s1_single_cycle_1_data_addr}),
    .data_in(s1_single_cycle_1_data_out), .clk(counter_1_out[3]), .we(s1_single_cycle_1_mem_we), .rclk(clk),
    .to_vram(u_video_to_vram), .vram_addr(u_video_vram_addr));
  not not_1 (not_1_out, u_video_to_vram);
  GraphicCard #(.graphicHeight(16), .graphicWidth(16)) graphiccard_1 (
    .A(u_video_vram_addr), .str(1'b1), .C(clk), .ld(1'b0), .B(1'b0), .D(not_1_out));

  // Notes on the sheet:
  //   clk: Hz: 4500
  //   in_2: default 1
  //   rom_1 loads out.bin
  //   rom_2 loads DMEM.hex
endmodule

/* Code of video:
module video(
    input [29:0] address,
    input [31:0] data_in,
    input clk, we, rclk,
    output to_vram,
    output [8:0] vram_addr
);
    reg [15:0] buffer [15:0];
    reg [15:0] vmem [15:0];
    reg [7:0] pointer = 0;
    
    int i;
    always_ff @(posedge clk) begin
        if(we) begin
            if((address[3])) begin
                for(i = 0; i <= 32; i = i + 1) vmem[i] <= buffer[i];
            end else begin buffer[{address[2:0], 1'b0}] <= data_in[31:16]; buffer[{address[2:0], 1'b1}] <= data_in[15:0]; end
        end
    end

    always_ff @(posedge rclk) begin
        pointer <= pointer + 1;
    end
    assign vram_addr = {1'b0, pointer};
    assign to_vram = vmem[pointer[7:4]][15-pointer[3:0]];

endmodule : video
*/
