// Digital circuit BAD_APPLE_MATRIX.dig as structural Verilog
module BAD_APPLE_MATRIX (
  input  clk,
  input  in_2,
  input  in_3
);

  wire s1_single_cycle_1_mem_we;
  wire [3:0] u_matrix_video_matrix_col_sel;
  wire [7:0] s1_single_cycle_1_inst_addr;
  wire [15:0] u_matrix_video_to_matrix;
  wire [23:0] s1_single_cycle_1_data_addr;
  wire [29:8] s1_single_cycle_1_inst_addr_2;
  wire [29:24] s1_single_cycle_1_data_addr_2;
  wire [31:0] rom_1_d, rom_2_d, s1_single_cycle_1_data_out;

  ROM #(.bigEndian("true"), .AddrBits(8), .Bits(32)) rom_1 (.A(s1_single_cycle_1_inst_addr), .sel(1'b1), .D(rom_1_d));
  ROM #(.bigEndian("true"), .AddrBits(24), .Bits(32)) rom_2 (.A(s1_single_cycle_1_data_addr), .sel(1'b1), .D(rom_2_d));
  s1_single_cycle s1_single_cycle_1 (
    .inst_in(rom_1_d), .clk(clk), .data_in(rom_2_d), .clk_en(in_2), .rst(in_3),
    .inst_addr({s1_single_cycle_1_inst_addr_2, s1_single_cycle_1_inst_addr}),
    .data_addr({s1_single_cycle_1_data_addr_2, s1_single_cycle_1_data_addr}),
    .data_out(s1_single_cycle_1_data_out), .mem_we(s1_single_cycle_1_mem_we));  // open: mask, mem_lock
  matrix_video #(.applicationType("IVERILOG"), .iverilogOptions("-g2012")) u_matrix_video (
    .address({s1_single_cycle_1_data_addr_2, s1_single_cycle_1_data_addr}),
    .data_in(s1_single_cycle_1_data_out), .clk(clk), .we(s1_single_cycle_1_mem_we),
    .to_matrix(u_matrix_video_to_matrix), .matrix_col_sel(u_matrix_video_matrix_col_sel));
  LedMatrix #(.ledPersistence("true"), .colAddrBits(4), .rowDataBits(16)) ledmatrix_1 (
    .rows(u_matrix_video_to_matrix), .column(u_matrix_video_matrix_col_sel));

  // Notes on the sheet:
  //   clk: Hz: 500
  //   in_2: default 1
  //   rom_1 loads out.bin
  //   rom_2 loads DMEM.hex
endmodule

/* Code of matrix_video:
module matrix_video(
    input [29:0] address,
    input [31:0] data_in,
    input clk, we,
    output [15:0] to_matrix,
    output [3:0] matrix_col_sel
);
    reg [15:0] buffer [15:0];
    reg [15:0] vmem [15:0];
    reg [3:0] cpointer = 0;
    int i;
    always_ff @(posedge clk) begin
        if(we) begin
            if((address[3])) begin
                for(i = 0; i <= 32; i = i + 1) vmem[i] <= buffer[i];
            end else begin buffer[{address[2:0], 1'b0}] <= data_in[31:16]; buffer[{address[2:0], 1'b1}] <= data_in[15:0]; end
        end
    end

    always_ff @(posedge clk) begin
        cpointer <= cpointer + 1;
    end
    assign matrix_col_sel = cpointer;
    assign to_matrix = {
        vmem[15][15-cpointer],
        vmem[14][15-cpointer],
        vmem[13][15-cpointer],
        vmem[12][15-cpointer],
        vmem[11][15-cpointer],
        vmem[10][15-cpointer],
        vmem[9][15-cpointer],
        vmem[8][15-cpointer],
        vmem[7][15-cpointer],
        vmem[6][15-cpointer],
        vmem[5][15-cpointer],
        vmem[4][15-cpointer],
        vmem[3][15-cpointer],
        vmem[2][15-cpointer],
        vmem[1][15-cpointer],
        vmem[0][15-cpointer]
    };

endmodule : matrix_video
*/
