// Digital circuit s1_single_cycle.dig as structural Verilog
module s1_single_cycle (
  input  [31:0] inst_in,
  input  clk,
  input  [31:0] data_in,
  input  clk_en,
  input  rst,
  output [29:0] inst_addr,
  output [29:0] data_addr,
  output [3:0] mask,
  output [31:0] data_out,
  output mem_we,
  output mem_lock
);

  wire alu_bsel, alu_modsel, and_1_out, brh, comparator_1_eq, comparator_1_lt, comparator_2_lt, imm_sel, jmp,
       multiplexer_6_out, or_1_out, or_2_out, reg_we, xor_1_out;
  wire [1:0] ip_sel, reg_insel, u_alu_res;
  wire [3:0] multiplexer_4_out;
  wire [8:7] u_inst_rom_control_word;
  wire [29:0] add_1_s, add_2_s, add_3_s, add_4_s, multiplexer_3_out;
  wire [31:0] bitextender_1_out, bitextender_2_out, bitextender_3_out, multiplexer_1_out, multiplexer_2_out,
       multiplexer_5_out, u_mem_adj_to_reg, u_regfile_rs1, u_regfile_rs2;

  regfile #(.applicationType("IVERILOG"), .iverilogOptions("-g2012")) u_regfile (
    .clk(clk), .we(reg_we), .clk_en(clk_en), .din(multiplexer_5_out), .rs1_addr(inst_in[20:16]),
    .rs2_addr(inst_in[11:7]), .rd_addr(inst_in[25:21]), .rs1(u_regfile_rs1), .rs2(u_regfile_rs2));
  ProgramCounter #(.applicationType("IVERILOG"), .iverilogOptions("-g2012")) u_ProgramCounter (
    .din(multiplexer_3_out), .clk_en(clk_en), .clk(clk), .jmp(or_2_out), .rst(rst), .dout(inst_addr));
  BitExtender #(.inputBits(12), .outputBits(32)) bitextender_1 (.in(inst_in[11:0]), .out(bitextender_1_out));
  BitExtender #(.inputBits(12), .outputBits(32)) bitextender_2 (
    .in({inst_in[25:21], inst_in[6:0]}), .out(bitextender_2_out));
  BitExtender #(.inputBits(21), .outputBits(32)) bitextender_3 (.in(inst_in[20:0]), .out(bitextender_3_out));
  Add #(.Bits(30)) add_1 (.a(bitextender_2_out[31:2]), .b(inst_addr), .c_i(1'b0), .s(add_1_s));  // open: c_o
  Add #(.Bits(30)) add_2 (.a(bitextender_3_out[31:2]), .b(inst_addr), .c_i(1'b0), .s(add_2_s));  // open: c_o
  Add #(.Bits(30)) add_3 (.a(u_regfile_rs1[31:2]), .b(bitextender_1_out[31:2]), .c_i(1'b0), .s(add_3_s));  // open: c_o
  Multiplexer #(.Bits(32)) multiplexer_1 (
    .sel(alu_bsel), .in_0(u_regfile_rs2), .in_1(multiplexer_2_out), .out(multiplexer_1_out));
  Multiplexer #(.Bits(32)) multiplexer_2 (
    .sel(imm_sel), .in_0(bitextender_1_out), .in_1(bitextender_2_out), .out(multiplexer_2_out));
  Add #(.Bits(30)) add_4 (.a(inst_addr), .b(30'h1), .c_i(1'b0), .s(add_4_s));  // open: c_o
  Multiplexer #(.Selector_Bits(2), .Bits(30)) multiplexer_3 (
    .sel(ip_sel), .in_0(add_1_s), .in_1(add_2_s), .in_2(add_3_s), .in_3({30{1'b0}}), .out(multiplexer_3_out));
  Multiplexer #(.Bits(4)) multiplexer_4 (
    .sel(alu_modsel), .in_0(inst_in[15:12]), .in_1(4'b0000), .out(multiplexer_4_out));
  alu #(.applicationType("IVERILOG"), .iverilogOptions("-g2012")) u_alu (
    .a(u_regfile_rs1), .b(multiplexer_1_out), .op(multiplexer_4_out), .res({data_addr, u_alu_res}));
  Multiplexer #(.Selector_Bits(2), .Bits(32)) multiplexer_5 (
    .sel(reg_insel), .in_0({data_addr, u_alu_res}), .in_1({inst_in[20:0], {11{1'b0}}}),
    .in_2(u_mem_adj_to_reg), .in_3({add_4_s, 2'b00}), .out(multiplexer_5_out));
  Comparator #(.Bits(32)) comparator_1 (
    .a(u_regfile_rs2), .b(bitextender_3_out), .eq(comparator_1_eq), .lt(comparator_1_lt));  // open: gt
  Comparator #(.Signed("true"), .Bits(32)) comparator_2 (
    .a(u_regfile_rs2), .b(bitextender_3_out), .lt(comparator_2_lt));  // open: gt, eq
  inst_rom #(.applicationType("IVERILOG"), .iverilogOptions("-g2012")) u_inst_rom (
    .opcode(inst_in[28:26]),
    .control_word({reg_insel, reg_we, u_inst_rom_control_word, ip_sel, brh, jmp, alu_modsel, imm_sel, alu_bsel}));
  mem_adj #(.applicationType("IVERILOG"), .iverilogOptions("-g2012")) u_mem_adj (
    .from_mem(data_in), .from_reg(u_regfile_rs2), .fn4(inst_in[15:12]), .addr_low(u_alu_res),
    .to_reg(u_mem_adj_to_reg), .to_mem(data_out), .mask(mask));
  Multiplexer #(.Selector_Bits(2)) multiplexer_6 (
    .sel(inst_in[13:12]), .in_0(comparator_1_eq), .in_1(comparator_1_lt), .in_2(comparator_2_lt),
    .in_3(1'b0), .out(multiplexer_6_out));
  xor xor_1 (xor_1_out, multiplexer_6_out, inst_in[14]);
  and and_1 (and_1_out, xor_1_out, brh);
  or or_1 (or_1_out, u_inst_rom_control_word[7], u_inst_rom_control_word[8]);
  or or_2 (or_2_out, and_1_out, jmp);
  and and_2 (mem_we, u_inst_rom_control_word[7], clk_en);
  and and_3 (mem_lock, or_1_out, clk_en);

  // Other names for the same wires on the sheet: imm_0_6[6:0] = inst_in[6:0]; rs2_addr[4:0] = inst_in[11:7];
  //   fn4[3:0] = inst_in[15:12]; rs1_addr[4:0] = inst_in[20:16]; rd_addr[4:0] = inst_in[25:21];
  //   opcode[2:0] = inst_in[28:26]
endmodule

/* Code of regfile:
module regfile(
    input clk, we, clk_en,
    input [31:0] din,
    input [4:0] rs1_addr, rs2_addr, rd_addr,
    output [31:0] rs1, rs2
);
    reg [31:0] memory [31:0];

    always_ff @(posedge clk) if(we && clk_en) memory[rd_addr] <= din;
    assign rs1 = (rs1_addr == 0) ? 32'h0 : memory[rs1_addr];
    assign rs2 = (rs2_addr == 0) ? 32'h0 : memory[rs2_addr];
endmodule : regfile
*/

/* Code of ProgramCounter:
module ProgramCounter(
    input wire [29:0] din,
    input wire clk_en,
    input wire clk,
    input wire jmp,
    input wire rst,
    output wire [29:0] dout
    
);

reg [29:0] ip = 0;
always_ff @(posedge clk) begin
    if(rst) ip <= 0;
    else if(jmp) ip <= din;
    else ip <= ip+1;
end

assign dout = ip;

endmodule
*/

/* Code of alu:
module alu(
    input [31:0] a, b,
    input [3:0] op,
    output reg [31:0] res
);

    wire [32:0] intermediate_addsub = a + {(b^{32{op[0]}})} + {31'b0, op[0]};
    always @* begin : operation
        case(op[2:0])
        3'h0: res = op[3] ? {31'b0, intermediate_addsub[32]} : intermediate_addsub[31:0];
        3'h1: res = op[3] ? {31'b0, !intermediate_addsub[32]} : intermediate_addsub[31:0];
        3'h2: res = a & b;
        3'h3: res = a | b;
        3'h4: res = a ^ b;
        3'h5: res = a >> b[4:0];
        3'h6: res = $signed(a) >>> b[4:0];
        3'h7: res = a << b[4:0];
        endcase
    end
endmodule : alu
*/

/* Code of inst_rom:
module inst_rom(
    input [2:0] opcode,
    output reg [11:0] control_word
);
    always_comb begin
        case(opcode)
        3'h0: control_word = 12'b00_1_0_0_00_0_0_0_0_0; //ALU
        3'h1: control_word = 12'b00_1_0_0_00_0_0_0_0_1; //ALUI
        3'h2: control_word = 12'b01_1_0_0_00_0_0_0_0_0; //LUI
        3'h3: control_word = 12'b00_0_0_1_00_0_0_1_1_1; //STORE
        3'h4: control_word = 12'b10_1_1_0_00_0_0_1_0_1; //LOAD
        3'h5: control_word = 12'b11_1_0_0_01_0_1_0_0_0; //JAL
        3'h6: control_word = 12'b11_1_0_0_10_0_1_0_0_0; //JALR
        3'h7: control_word = 12'b00_0_0_0_00_1_0_0_0_0; //COND JMP
        endcase
    end
endmodule : inst_rom
*/

/* Code of mem_adj:
module mem_adj(
    input [31:0] from_mem, from_reg,
    input [3:0] fn4,
    input [1:0] addr_low,
    output reg [31:0] to_reg, to_mem,
    output reg [3:0] mask
);

logic [7:0] adj_byte;
logic [15:0] adj_word;
wire [1:0] size = fn4[1:0];

always @* begin : Word_And_Byte_Adj
    case(addr_low)
    2'h0: begin adj_byte = from_mem[31:24]; adj_word = from_mem[31:16]; end
    2'h1: begin adj_byte = from_mem[23:16]; adj_word = from_mem[31:16]; end
    2'h2: begin adj_byte = from_mem[15:8]; adj_word = from_mem[15:0]; end
    2'h3: begin adj_byte = from_mem[7:0]; adj_word = from_mem[15:0]; end
    endcase
end

always @* begin : Input_Format_Sel
    case(size)
    2'h0: to_reg = {{24{adj_byte[7] & fn4[3]}}, adj_byte};
    2'h1: to_reg = {{16{adj_word[15] & fn4[3]}}, adj_word};
    2'h2: to_reg = from_mem;
    2'h3: to_reg = from_mem;
    endcase
end

always @* begin : OutputAdj_and_Mask
    to_mem = 32'h0;
    mask = 4'h0;
    if(fn4 == 0) begin
        case(addr_low)
        2'h0: begin to_mem = {from_reg[7:0], 24'h0}; mask = 4'b1000; end
        2'h1: begin to_mem = {8'h0, from_reg[7:0], 16'h0}; mask = 4'b0100; end
        2'h2: begin to_mem = {16'h0, from_reg[7:0], 8'h0}; mask = 4'b0010; end
        2'h3: begin to_mem = {24'h0, from_reg[7:0]}; mask = 4'b0001; end
        endcase
    end else if(fn4 == 1) begin
        case(addr_low)
        2'h0, 2'h1: begin to_mem = {from_reg[15:0], 16'h0}; mask = 4'b1100; end
        2'h2, 2'h3: begin to_mem = {16'h0, from_reg[15:0]}; mask = 4'b0011; end
        endcase
    end else if((fn4 == 2) || (fn4 == 3)) begin to_mem = from_reg; mask = 4'b1111; end;
end

endmodule : mem_adj

//Note: Use negedge flip flop in Word_and_Byte adj to prevent circling problems
*/
