// Digital circuit SRM_Basic1.dig as structural Verilog
module SRM_Basic1 (
  input  Res,
  input  H_int,
  input  En,
  input  [31:0] D_in,
  input  clk,
  output [31:0] D_out,
  output MR,
  output [21:0] Address,
  output clk2,
  output mem_we,
  output Int_en
);

  wire and_1_out, Cache_fetch, jmp, m_req, not_1_out;
  wire [21:0] d_addr, i_addr;
  wire [23:0] cache_addr;
  wire [23:2] srm_core_1_next_jmp;
  wire [31:0] cache_out, register_1_q, u_icache_dout;

  icache #(.applicationType("IVERILOG"), .iverilogOptions("-g2012")) u_icache (
    .clk(clk), .req(En), .we(mem_we), .addr({i_addr, 2'b00}), .dw_addr({d_addr, 2'b00}), .din(D_in),
    .jmp(jmp), .jmp_addr({srm_core_1_next_jmp, 2'b00}), .addr_out(cache_addr), .dout(u_icache_dout),
    .fetch(Cache_fetch));
  Register #(.Bits(32)) register_1 (.D(u_icache_dout), .C(clk), .en(~mem_we), .Q(register_1_q));
  Multiplexer #(.Bits(32)) multiplexer_1 (.sel(mem_we), .in_0(u_icache_dout), .in_1(register_1_q), .out(cache_out));
  not not_1 (not_1_out, Cache_fetch);
  and and_1 (and_1_out, En, not_1_out);
  SRM_core srm_core_1 (
    .clk(clk), .En(and_1_out), .Res(Res), .H_int(H_int), .D_in(D_in), .I_in(cache_out), .clk2(clk2),
    .MEM_req(m_req), .MEM_we(mem_we), .D_Addr(d_addr), .D_out(D_out), .I_Addr(i_addr), .jmp(jmp),
    .int_en(Int_en), .next_jmp(srm_core_1_next_jmp));
  or or_1 (MR, m_req, Cache_fetch);
  Multiplexer #(.Bits(22)) multiplexer_2 (.sel(Cache_fetch), .in_0(d_addr), .in_1(cache_addr[23:2]), .out(Address));

  // Other names for the same wires on the sheet: CPU_en = En; CPU_int = H_int; CPU_res = Res
endmodule

/* Code of icache:
module icache(
    input clk,
    input req,
    input we,
    input [23:0] addr,
    input [23:0] dw_addr,
    input [31:0] din,
    input jmp,
    input [23:0] jmp_addr,
    output [23:0] addr_out,
    output reg [31:0] dout,
    output fetch
);

reg [14:0] tag [15:0];
reg [31:0] cache [255:0];
logic miss;
logic [7:0] cache_addr;
reg [3:0] low_pointer = 0;
reg stall;
logic cache_we;

initial begin
    dout = 0;
end
reg jms = 0;

always_ff @(posedge clk) begin
if(!stall) jms <= jmp;
if(jmp || fetch) dout <= cache[cache_addr];
else dout <= cache[cache_addr + 1];
    if(cache_we) begin
        cache[cache_addr] <= din;
    end
end

always @* begin
    cache_we = miss;
    if({1'b1, addr[23:10]} == tag[addr[9:6]]) begin
        miss = 0;
    end else begin
        miss = req && 1;
    end
    if(miss) cache_addr = {((jmp || jms) ? jmp_addr[9:6] : addr[9:6]), low_pointer};
    else cache_addr = jmp ? jmp_addr[9:2] : addr[9:2];
end

always_ff @(posedge clk) begin
    stall <= miss;
    if(miss) begin
        low_pointer <= low_pointer + 1;
        if(low_pointer == 15) begin
            tag[jmp ? jmp_addr : addr[9:6]] <= {1'b1, ((jmp || jms) ? jmp_addr[23:10] : addr[23:10])};
        end
    end
    if(!req && we && !miss) begin
        tag[dw_addr[9:6]] <= 0;
    end
end

assign addr_out = {addr[23:6], low_pointer, 2'b00};
assign fetch = miss || stall;

endmodule
*/
