// Digital circuit SRM_TestPC1.dig as structural Verilog
module SRM_TestPC1 (
  input  in_1,
  input  in_2,
  input  clk,
  output out_4
);

  wire srm_basic1_1_clk2, srm_basic1_1_mem_we, srm_basic1_1_mr, telnet_int, u_periferals_tty_rd,
       u_periferals_tty_str;
  wire [7:0] telnet_1_out, u_periferals_tty_out;
  wire [20:0] u_periferals_rom_addr;
  wire [21:0] srm_basic1_1_address;
  wire [31:0] rom_1_d, srm_basic1_1_d_out, u_periferals_dout;

  SRM_Basic1 srm_basic1_1 (
    .Res(in_1), .H_int(telnet_int), .En(in_2), .D_in(u_periferals_dout), .clk(clk),
    .D_out(srm_basic1_1_d_out), .MR(srm_basic1_1_mr), .Address(srm_basic1_1_address),
    .clk2(srm_basic1_1_clk2), .mem_we(srm_basic1_1_mem_we), .Int_en(out_4));
  periferals #(.applicationType("IVERILOG"), .iverilogOptions("-g2012")) u_periferals (
    .clk(srm_basic1_1_clk2), .req(srm_basic1_1_mr), .din(srm_basic1_1_d_out), .addr(srm_basic1_1_address),
    .we(srm_basic1_1_mem_we), .rom_in(rom_1_d), .tty_in(telnet_1_out), .dout(u_periferals_dout),
    .rom_addr(u_periferals_rom_addr), .tty_out(u_periferals_tty_out), .tty_str(u_periferals_tty_str),
    .tty_rd(u_periferals_tty_rd));
  Telnet telnet_1 (
    .in(u_periferals_tty_out), .C(srm_basic1_1_clk2), .wr(u_periferals_tty_str), .rd(u_periferals_tty_rd),
    .out(telnet_1_out), .av(telnet_int));
  ROM #(.bigEndian("true"), .AddrBits(21), .isProgramMemory("true"), .Bits(32)) rom_1 (
    .A(u_periferals_rom_addr), .sel(1'b1), .D(rom_1_d));
  PullDown #(.Bits(8)) pulldown_1 (.out(telnet_1_out));

  // Notes on the sheet:
  //   in_2: default 1
  //   clk: Hz: 1000
  //   rom_1 loads out.bin
endmodule

/* Code of periferals:
module periferals(
    input clk,
    input req,
    input [31:0] din,
    input [21:0] addr,
    input we,
    input [31:0] rom_in,
    input [7:0] tty_in,
    output reg [31:0] dout,
    output [20:0] rom_addr,
    output [7:0] tty_out,
    output tty_str,
    output tty_rd
);

initial dout = 0;

assign rom_addr = addr[20:0];
reg [31:0] memory [4194303:0];

always_ff @(posedge clk) begin
    if(we) begin
        if((addr >= 22'b1000000000000000000000) && (addr <= 22'b1111111111111111111110)) memory[addr] <= din;
    end
end

always_ff @(posedge clk) begin
    if((addr >= 22'b0) && (addr <= 22'h1fffff)) dout <= rom_in;
    else if(addr == 22'h3fffff) dout <= {24'h0, tty_in};
    else dout <= memory[addr];
end

assign tty_out = din[31:24];
assign tty_str = (addr == 22'b1111111111111111111111) && we;
assign tty_rd = (addr == 22'b1111111111111111111111) && req;

endmodule
*/
