// Digital circuit SRM_core.dig as structural Verilog
module SRM_core (
  input  clk,
  input  En,
  input  Res,
  input  H_int,
  input  [31:0] D_in,
  input  [31:0] I_in,
  output clk2,
  output MEM_req,
  output MEM_we,
  output [21:0] D_Addr,
  output [31:0] D_out,
  output [21:0] I_Addr,
  output jmp,
  output int_en,
  output [21:0] next_jmp
);

  wire and_1_out, and_2_out, d_ff_1_nq, int_av, ir_tsf, ks, mem_we_t, not_1_out, r_cwe, u_int_wait_int_mode;
  wire [3:0] fn1, sub_flags;
  wire [4:0] r_asel, r_bsel, r_csel;
  wire [13:0] u_inst_decoder_control_lines;
  wire [31:0] alu_b, alu_res, ir, pc, pc_in, r_in, reg_aout, reg_bout, u_connections_d_addr;

  int_wait #(.applicationType("IVERILOG"), .iverilogOptions("-g2012")) u_int_wait (
    .h_int(H_int), .clk(clk), .av(int_av), .int_mode(u_int_wait_int_mode));
  and and_1 (and_1_out, int_en, u_int_wait_int_mode, int_av);
  inst_decoder #(.applicationType("IVERILOG"), .iverilogOptions("-g2012")) u_inst_decoder (
    .en(En), .int_en(int_en), .opcode(I_in[31:27]), .sub_flags(sub_flags), .func_1(fn1),
    .hardware_int(and_1_out), .control_lines(u_inst_decoder_control_lines));
  and and_2 (and_2_out, d_ff_1_nq, mem_we_t);
  connections #(.applicationType("IVERILOG"), .iverilogOptions("-g2012")) u_connections (
    .control_lines(u_inst_decoder_control_lines), .inst_bus(I_in), .din(D_in), .alu_res(alu_res),
    .reg_bout(reg_bout), .reg_aout(reg_aout), .pc({pc[31:24], I_Addr, pc[1:0]}), .ir(ir), .reg_c_we(r_cwe),
    .jmp(jmp), .mem_we(mem_we_t), .ir_tsf(ir_tsf), .mem_req(MEM_req), .ks(ks), .fn1(fn1), .reg_asel(r_asel),
    .reg_bsel(r_bsel), .reg_csel(r_csel), .alu_b_in(alu_b), .reg_din(r_in),
    .pc_din({pc_in[31:24], next_jmp, pc_in[1:0]}),
    .d_addr({u_connections_d_addr[31:24], D_Addr, u_connections_d_addr[1:0]}), .dout(D_out));
  D_FF d_ff_1 (.D(and_2_out), .C(clk), .Q(MEM_we), .nQ(d_ff_1_nq));
  not not_1 (not_1_out, and_2_out);
  not not_2 (clk2, clk);
  regfile #(.applicationType("IVERILOG"), .iverilogOptions("-g2012")) u_regfile (
    .din(r_in), .clk(clk), .c_we(r_cwe), .ir_tsf(ir_tsf), .ks(ks), .asel(r_asel), .bsel(r_bsel),
    .csel(r_csel), .pc({pc[31:24], I_Addr, pc[1:0]}), .aout(reg_aout), .bout(reg_bout), .ir(ir),
    .int_en(int_en));
  alu #(.applicationType("IVERILOG"), .iverilogOptions("-g2012")) u_alu (
    .a(reg_aout), .b(alu_b), .op(fn1), .res(alu_res), .sub_flags(sub_flags));
  and and_3 (int_av, En, not_1_out);
  ProgramCounter #(.applicationType("IVERILOG"), .iverilogOptions("-g2012")) u_ProgramCounter (
    .din({pc_in[31:24], next_jmp, pc_in[1:0]}), .we(int_av), .clk(clk), .jmp(jmp), .rst(Res),
    .dout({pc[31:24], I_Addr, pc[1:0]}));

  // Other names for the same wires on the sheet: inst_bus[31:0] = I_in; mem_out[31:0] = D_in; pc[23:2] = I_Addr;
  //   pc_in[23:2] = next_jmp; pc_jmp = jmp; pc_rst = Res

  // Notes on the sheet:
  //   En: default 1
endmodule

/* Code of int_wait:
module int_wait(
    input h_int,
    input clk,
    input av,
    output int_mode
);

reg state = 0;
reg [2:0] wait_ctr = 0;

always_ff @(posedge clk) begin
    if(av) begin
        if(h_int) wait_ctr <= wait_ctr + 1;
        else wait_ctr <= 0;
        if(wait_ctr == 7) state <= h_int;
        else state <= 0;
    end
end

assign int_mode = state && av;

endmodule
*/

/* Code of inst_decoder:
module inst_decoder(
    input en,
    input int_en,
    input [4:0] opcode,
    input [3:0] sub_flags,
    input [3:0] func_1,
    input hardware_int,
    output [13:0] control_lines
);
wire [7:0] cond = {~sub_flags, sub_flags};
wire [1:0] fsel = func_1[1:0];
wire fout = cond[{func_1[2:0]}];
logic [13:0] intermediate_lines;
always_comb begin
    if(!(hardware_int && int_en)) begin
        case(opcode)
        5'h0: intermediate_lines = 14'b00000000000001; //ALU
        5'h1: intermediate_lines = 14'b00000000000011; //ALUI
        5'h2: intermediate_lines = 14'b00000100000001; //LUI
        5'h3: intermediate_lines = 14'b00000000001000; //Store
        5'h4: intermediate_lines = 14'b10011000000001; //Load
        5'h5: intermediate_lines = 14'b00000001000100; //IJR
        5'h6: intermediate_lines = 14'b00000000000100; //JMP
        5'h7: intermediate_lines = {11'b00000000100, fout, 2'b00}; //COND JMP
        5'h8: intermediate_lines = 14'b10100001110100; //SYSCALL
        default: intermediate_lines = 0;
        endcase
    end else begin
        intermediate_lines = 14'b11110001110100;
    end
end
assign control_lines = (en) ? intermediate_lines : 0;

endmodule

//0. C_WE
//1. ALU_Bsel
//2. PC_JMP
//3. MEM_WE
//4. KS
//5-7. PC_IN: JMP, COND_JMP, IJR, DB_In, IR
//8-9. REG_IN: ALU, UPPER_IMM, MEM
//10-11. MEM_ADDR: Store, Load, S_INT, H_INT
//12. IR_tsf
//13. Mem_REQ
*/

/* Code of connections:
module connections(
    input [13:0] control_lines,
    input [31:0] inst_bus,
    input [31:0] din,
    input [31:0] alu_res,
    input [31:0] reg_bout,
    input [31:0] reg_aout,
    input [31:0] pc,
    input [31:0] ir,
    //Control lines
    output reg_c_we,
    output jmp,
    output mem_we,
    output ir_tsf,
    output mem_req,
    output ks,
    //Control buses
    output [3:0] fn1,
    output [4:0] reg_asel,
    output [4:0] reg_bsel,
    output [4:0] reg_csel,
    //Data buses
    output [31:0] alu_b_in,
    output logic [31:0] reg_din,
    output logic [31:0] pc_din,
    output logic [31:0] d_addr,
    output logic [31:0] dout
);

assign debug1 = byte_adj_out;
assign debug2 = addr_byte_sel;

assign reg_c_we = control_lines[0];
assign jmp = control_lines[2];
assign mem_we = control_lines[3];
assign ks = control_lines[4];
assign ir_tsf = control_lines[12];
assign mem_req = control_lines[13];

assign fn1 = inst_bus[16:13];
assign reg_asel = inst_bus[21:17];
assign reg_csel = inst_bus[26:22];
assign reg_bsel = inst_bus[12:8];

assign alu_b_in = control_lines[1] ? {19'h0, inst_bus[12:0]} : reg_bout;

wire [1:0] reg_in_sel = control_lines[9:8];
wire [2:0] pc_in_sel = control_lines[7:5];
wire [1:0] daddr_sel = control_lines[11:10];
logic [31:0] store_addr;
logic [31:0] load_addr;
logic [31:0] adjusted_din;

logic [7:0] byte_in;
logic [15:0] word_in;
logic [31:0] byte_adj_out;
logic [31:0] word_adj_out;

wire [1:0] addr_byte_sel = d_addr[1:0];
wire addr_word_sel = d_addr[1];

wire [1:0] low_fn1 = fn1[1:0];


always @* begin
    case(pc_in_sel)             //PC in sel
    3'b000: pc_din = pc + {{5{inst_bus[26]}}, inst_bus[26:0]};
    3'b001: pc_din = pc + {{19{inst_bus[26]}}, inst_bus[26:22], inst_bus[7:0]};
    3'b010: pc_din = reg_aout + {{19{inst_bus[26]}}, inst_bus[26:22], inst_bus[16:0]};
    3'b011: pc_din = din;
    3'b100: pc_din = ir;
    default: pc_din = 0;
    endcase
end

always @* begin
    case(daddr_sel)             //Addr sel
    2'b00: d_addr = store_addr;
    2'b01: d_addr = load_addr;
    2'b10: d_addr = 0;
    2'b11: d_addr = 4;
    endcase
end

always @* begin
    case(low_fn1)               //Address alignment
    2'h0: begin
        store_addr = reg_aout + {{19{inst_bus[26]}}, inst_bus[26:22], inst_bus[7:0]};
        load_addr = reg_aout + {{19{inst_bus[12]}}, inst_bus[12:0]};
    end
    2'h1: begin
        store_addr = reg_aout + {{19{inst_bus[26]}}, inst_bus[26:22], inst_bus[7:1], 1'b0};
        load_addr = reg_aout + {{19{inst_bus[12]}}, inst_bus[12:1], 1'b0};
    end
    2'h2: begin
        store_addr = reg_aout + {{19{inst_bus[26]}}, inst_bus[26:22], inst_bus[7:2], 2'b0};
        load_addr = reg_aout + {{19{inst_bus[12]}}, inst_bus[12:2], 2'b0};
    end
    default: begin
        store_addr = 0;
        load_addr = 0;
    end
    endcase
end

always @* begin
    case(addr_byte_sel)         //Adjust byte din
    2'b00: byte_in = din[31:24];
    2'b01: byte_in = din[23:16];
    2'b10: byte_in = din[15:8];
    2'b11: byte_in = din[7:0];
    endcase
    case(addr_word_sel)         //Adjust word din
    1'b0: word_in = din[31:16];
    1'b1: word_in = din[15:0];
    endcase
end

always @* begin
    case(low_fn1)               //Select data in type
    2'h0: adjusted_din = {{24{byte_in[7] && fn1[2]}}, byte_in};
    2'h1: adjusted_din = {{16{word_in[15] && fn1[2]}}, word_in};
    2'h2: adjusted_din = din;
    default: adjusted_din = 0;
    endcase
end

always @* begin
    case(reg_in_sel)            //Reg in sel
    2'b00: reg_din = alu_res;
    2'b01: reg_din = inst_bus[21:0] << 10;
    2'b10: reg_din = adjusted_din;
    2'b11: reg_din = adjusted_din;
    endcase
end

always @* begin
    case(low_fn1)
    2'b00: dout = byte_adj_out;
    2'b01: dout = word_adj_out;
    2'b10: dout = reg_bout;
    2'b11: dout = 0;
    endcase
end

always @* begin
    case(addr_byte_sel)         //Adjust data out with bytes
    2'b00: byte_adj_out = {reg_bout[7:0], din[23:0]};
    2'b01: byte_adj_out = {din[31:24], reg_bout[7:0], din[15:0]};
    2'b10: byte_adj_out = {din[31:16], reg_bout[7:0], din[7:0]};
    2'b11: byte_adj_out = {din[31:8], reg_bout[7:0]};
    endcase
    case(addr_word_sel)
    1'b0: word_adj_out = {reg_bout[15:0], din[15:0]};
    1'b1: word_adj_out = {din[23:16], reg_bout[15:0]};
    endcase
end

endmodule

//0. C_WE
//1. ALU_Bsel
//2. PC_JMP
//3. MEM_WE
//4. KS
//5-7. PC_IN: JMP, COND_JMP, IJR, DB_In, IR
//8-9. REG_IN: ALU, UPPER_IMM, MEM
//10-11. MEM_ADDR: Store, Load, S_INT, H_INT
//12. IR_tsf
//13. Mem_REQ
*/

/* Code of regfile:
module regfile(
    input [31:0] din,
    input clk,
    input c_we,
    input ir_tsf,
    input ks,
    input [4:0] asel,
    input [4:0] bsel,
    input [4:0] csel,
    input [31:0] pc,
    output logic [31:0] aout,
    output logic [31:0] bout,
    output [31:0] ir,
    output int_en
);

initial memory[1] = 1;

reg [31:0] memory [31:0];
always_ff @(posedge clk) begin
    if(c_we) begin
        if(csel == 1) begin
            if(memory[1][0]) memory[1] <= din;
        end else memory[csel] <= din;
    end
    if(ir_tsf) memory[3] <= pc;
end

always_ff @(posedge clk) begin
    if(ks) begin
        memory[1][0] <= 1;
    end
end

always_comb begin
    case(asel)
    5'h0: aout = 0;
    5'h2: aout = pc;
    default: aout = memory[asel];
    endcase
    case(bsel)
    5'h0: bout = 0;
    5'h2: bout = pc;
    default: bout = memory[bsel];
    endcase
end

assign ir = memory[3];
assign int_en = memory[1][1];

endmodule
*/

/* Code of alu:
module alu(
    input [31:0] a,
    input [31:0] b,
    input [3:0] op,
    output logic [31:0] res,
    output [3:0] sub_flags
);

always_comb begin
    case(op)
    4'h0: res = final_addition;
    4'h1: res = final_subtraction;
    4'h2: res = a & b;
    4'h3: res = a | b;
    4'h4: res = a ^ b;
    4'h5: res = a >> b;
    4'h6: res = a >>> b;
    4'h7: res = a << b;
    4'h8: res = {31'h0, add_carry};
    4'h9: res = {31'h0, sub_borrow};
    default: res = 0;
    endcase
end

wire [32:0] intermediate_addition = {1'b0, a} + {1'b0, b};
wire [32:0] intermediate_subtraction = {1'b0, a} - {1'b0, b};
wire sub_borrow = intermediate_subtraction[32];
wire add_carry = intermediate_addition[32];
wire [31:0] final_addition = intermediate_addition[31:0];
wire [31:0] final_subtraction = intermediate_subtraction[31:0];

assign sub_flags = {((a[31] == b[31]) && (final_subtraction[31] != a[31])), intermediate_subtraction[31], sub_borrow, {!(|(a - b))}}; //zero, borrow, sign, overflow

endmodule : alu
*/

/* Code of ProgramCounter:
module ProgramCounter(
    input wire [31:0] din,
    input wire we,
    input wire clk,
    input wire jmp,
    input wire rst,
    output wire [31:0] dout
    
);

reg [31:0] pc = 8;
always_ff @(posedge clk) begin
    if(we) begin
        if(!jmp && !rst) begin
            pc <= pc + 4;
        end
        if(jmp && !rst) begin
            pc <= din;
        end
        if(rst) begin
            pc <= 0;
        end
    end
end

assign dout = pc;

endmodule
*/
