// Digital circuit SRM.dig as structural Verilog
module SRM (
  input  in_1,
  input  in_2,
  input  in_3,
  input  in_4,
  input  clk,
  output [31:0] out_5,
  output [31:0] out_6,
  output [14:0] out_7,
  output [21:0] out_8,
  output [31:0] out_9,
  output [3:0] out_11,
  output [3:0] out_12,
  output [31:0] out_13,
  output [31:0] out_14,
  output [31:0] out_15,
  output [31:0] out_16,
  output [1:0] out_17,
  output [7:0] out_18
);

  wire ir_tsf, ks, mem_req, mem_we, not_1_out, pc_jmp, r_cwe, sr_in, sr_we;
  wire [1:0] sr_sel;
  wire [3:0] sr;
  wire [4:0] r_asel, r_bsel, r_csel;
  wire [31:0] alu_res, ir, pc, pc_in, reg_bout;

  inst_decoder #(.applicationType("IVERILOG"), .iverilogOptions("-g2012")) u_inst_decoder (
    .en(in_3), .int_en(sr[1]), .opcode(out_5[31:27]), .sub_flags(out_11), .func_1(out_12),
    .hardware_int(in_4), .control_lines(out_7));
  ROM #(.bigEndian("true"), .AddrBits(22), .isProgramMemory("true"), .Bits(32)) rom_1 (
    .A(out_8), .sel(1'b1), .D(out_5));
  connections #(.applicationType("IVERILOG"), .iverilogOptions("-g2012")) u_connections (
    .control_lines(out_7), .inst_bus(out_5), .din(out_15), .alu_res(alu_res), .reg_bout(reg_bout),
    .reg_aout(out_13), .pc({pc[31:24], out_8, pc[1:0]}), .ir(ir), .reg_c_we(r_cwe), .jmp(pc_jmp),
    .sr_we(sr_we), .mem_we(mem_we), .ks(ks), .ir_tsf(ir_tsf), .mem_req(mem_req), .fn1(out_12), .sr_in(sr_in),
    .reg_asel(r_asel), .reg_bsel(r_bsel), .reg_csel(r_csel), .sr_sel(sr_sel), .alu_b_in(out_14),
    .reg_din(out_6), .pc_din(pc_in), .d_addr(out_16), .dout(out_9), .fn_1_low(out_17), .byteadj_out(out_18));
  not not_1 (not_1_out, clk);
  regfile #(.applicationType("IVERILOG"), .iverilogOptions("-g2012")) u_regfile (
    .din(out_6), .clk(clk), .c_we(r_cwe), .ir_tsf(ir_tsf), .sr_in(sr_in), .sr_we(sr_we), .ks(ks),
    .sr_sel(sr_sel), .asel(r_asel), .bsel(r_bsel), .csel(r_csel), .pc({pc[31:24], out_8, pc[1:0]}),
    .aout(out_13), .bout(reg_bout), .ir(ir), .sr(sr));
  ProgramCounter #(.applicationType("IVERILOG"), .iverilogOptions("-g2012")) u_ProgramCounter (
    .din(pc_in), .we(in_3), .clk(clk), .jmp(pc_jmp), .rst(in_2), .dout({pc[31:24], out_8, pc[1:0]}));
  BlockRAMDualPort #(.AddrBits(22), .Bits(32)) blockramdualport_1 (
    .A(out_16[23:2]), .Din(out_9), .str(mem_we), .C(not_1_out), .D(out_15));
  alu #(.applicationType("IVERILOG"), .iverilogOptions("-g2012")) u_alu (
    .a(out_13), .b(out_14), .op(out_12), .res(alu_res), .sub_flags(out_11));

  // Other names for the same wires on the sheet: alu_b[31:0] = out_14; en = in_3; fn1[3:0] = out_12;
  //   inst_bus[31:0] = out_5; mem_out[31:0] = out_15; pc[23:2] = out_8; pc_rst = in_2; r_in[31:0] = out_6;
  //   reg_aout[31:0] = out_13; sub_flags[3:0] = out_11; Φ = clk

  // Notes on the sheet:
  //   clk: Hz: 32
  //   rom_1 loads out.bin
endmodule

/* Code of inst_decoder:
module inst_decoder(
    input en,
    input int_en,
    input [4:0] opcode,
    input [3:0] sub_flags,
    input [3:0] func_1,
    input hardware_int,
    output [14:0] control_lines
);
wire [7:0] cond = {~sub_flags, sub_flags};
wire [1:0] fsel = func_1[1:0];
wire fout = cond[{func_1[2:0]}];
logic [14:0] intermediate_lines;
always_comb begin
    if(!(hardware_int && int_en)) begin
        case(opcode)
        5'h0: intermediate_lines = 15'b000000000000001; //ALU
        5'h1: intermediate_lines = 15'b000000000000011; //ALUI
        5'h2: intermediate_lines = 15'b000001000000001; //LUI
        5'h3: intermediate_lines = 15'b000000000010000; //Store
        5'h4: intermediate_lines = 15'b100110000000001; //Load
        5'h5: intermediate_lines = 15'b000000010000100; //IJR
        5'h6: intermediate_lines = 15'b000000000000100; //JMP
        5'h7: intermediate_lines = {12'b000000001000, fout, 2'b00}; //COND JMP
        5'h8: intermediate_lines = 15'b101000011100100; //SYSCALL
        5'h9: intermediate_lines = 15'b000000000001000; //SSB-CSB
        default: intermediate_lines = 0;
        endcase
    end else begin
        intermediate_lines = 16'b1011000110100100;
    end
end
assign control_lines = (en) ? intermediate_lines : 0;
endmodule
//0. C_WE
//1. ALU_Bsel
//2. PC_JMP
//3. SR_WE
//4. MEM_WE
//5. KS
//6-8. PC_IN: JMP, COND_JMP, IJR, DB_In, IRD
//9-10. REG_IN: ALU, UPPER_IMM, MEM
//11-12. MEM_ADDR: Store, Load, S_INT, H_INT
//13. IRD_tsf
//14. Mem_REQ
*/

/* Code of connections:
module connections(
    input [14:0] control_lines,
    input [31:0] inst_bus,
    input [31:0] din,
    input [31:0] alu_res,
    input [31:0] reg_bout,
    input [31:0] reg_aout,
    input [31:0] pc,
    input [31:0] ir,
    //Control lines
    output reg_c_we,
    output jmp,
    output sr_we,
    output mem_we,
    output ks,
    output ir_tsf,
    output mem_req,
    //Control buses
    output [3:0] fn1,
    output sr_in,
    output [4:0] reg_asel,
    output [4:0] reg_bsel,
    output [4:0] reg_csel,
    output [1:0] sr_sel,
    //Data buses
    output [31:0] alu_b_in,
    output reg [31:0] reg_din,
    output reg [31:0] pc_din,
    output reg [31:0] d_addr,
    output reg [31:0] dout,
    //
    output [1:0] fn_1_low,
    output [7:0] byteadj_out
);
assign fn_1_low = reg_in_sel;
assign byteadj_out = adjusted_din;

assign reg_c_we = control_lines[0];
assign jmp = control_lines[2];
assign sr_we = control_lines[3];
assign mem_we = control_lines[4];
assign ks = control_lines[5];
assign ir_tsf = control_lines[13];
assign mem_req = control_lines[14];

assign fn1 = inst_bus[16:13];
assign sr_in = inst_bus[22];
assign reg_asel = inst_bus[21:17];
assign reg_csel = inst_bus[26:22];
assign reg_bsel = inst_bus[12:8];
assign sr_sel = inst_bus[26:23];

assign alu_b_in = control_lines[1] ? {19'h0, inst_bus[12:0]} : reg_bout;

wire [1:0] reg_in_sel = control_lines[10:9];
wire [2:0] pc_in_sel = control_lines[8:6];
wire [1:0] daddr_sel = control_lines[12:11];
reg [31:0] store_addr;
reg [31:0] load_addr;
reg [31:0] adjusted_din;

reg [7:0] byte_in;
reg [15:0] word_in;
reg [7:0] byte_adj_out;
reg [15:0] word_adj_out;

wire [1:0] addr_byte_sel = d_addr[1:0];
wire addr_word_sel = d_addr[1];

wire [1:0] low_fn1 = fn1[1:0];


always @* begin
    case(reg_in_sel)            //Reg in sel
    2'b00: reg_din = alu_res;
    2'b01: reg_din = inst_bus[21:0] << 10;
    2'b10: reg_din = adjusted_din;
    2'b11: reg_din = adjusted_din;
    endcase
    case(pc_in_sel)             //PC in sel
    3'b000: pc_din = pc + {{5{inst_bus[26]}}, inst_bus[26:0]};
    3'b001: pc_din = pc + {{19{inst_bus[26]}}, inst_bus[26:22], inst_bus[7:0]};
    3'b010: pc_din = reg_aout + {{19{inst_bus[26]}}, inst_bus[26:22], inst_bus[16:0]};
    3'b011: pc_din = din;
    3'b100: pc_din = ir;
    default: pc_din = 0;
    endcase
    case(daddr_sel)             //Addr sel
    2'b00: d_addr = store_addr;
    2'b01: d_addr = load_addr;
    2'b10: d_addr = 0;
    2'b11: d_addr = 4;
    endcase
    case(low_fn1)               //Address alignment
    2'h0: begin
        store_addr = reg_aout + {{19{inst_bus[26]}}, inst_bus[26:22], inst_bus[7:0]};
        load_addr = reg_aout + {{19{inst_bus[12]}}, inst_bus[12:0]};
    end
    2'h1: begin
        store_addr = reg_aout + {{19{inst_bus[26]}}, inst_bus[26:22], inst_bus[7:1], 1'b0};
        load_addr = reg_aout + {{19{inst_bus[12]}}, inst_bus[12:1], 1'b0};
    end
    2'h2: begin
        store_addr = reg_aout + {{19{inst_bus[26]}}, inst_bus[26:22], inst_bus[7:2], 2'b0};
        load_addr = reg_aout + {{19{inst_bus[12]}}, inst_bus[12:2], 2'b0};
    end
    default: begin
        store_addr = 0;
        load_addr = 0;
    end
    endcase
    case(addr_byte_sel)         //Adjust byte din
    2'b00: byte_in = din[31:24];
    2'b01: byte_in = din[23:16];
    2'b10: byte_in = din[15:8];
    2'b11: byte_in = din[7:0];
    endcase
    case(addr_word_sel)         //Adjust word din
    1'b0: word_in = din[31:16];
    1'b1: word_in = din[15:0];
    endcase
    case(low_fn1)               //Select data in type
    2'b00: adjusted_din = {24'b0, byte_in};
    2'b01: adjusted_din = {16'b0, word_in};
    2'b10: adjusted_din = din;
    default: adjusted_din = 0;
    endcase
    case(addr_byte_sel)         //Adjust data out with bytes
    2'b00: byte_adj_out = {reg_bout[7:0], din[23:0]};
    2'b01: byte_adj_out = {din[31:24], reg_bout[7:0], din[15:0]};
    2'b10: byte_adj_out = {din[31:16], reg_bout[7:0], din[7:0]};
    2'b11: byte_adj_out = {din[31:8], reg_bout[7:0]};
    endcase
    case(addr_word_sel)
    1'b0: word_adj_out = {reg_bout[15:0], din[15:0]};
    1'b1: word_adj_out = {din[23:16], reg_bout[15:0]};
    endcase
    case(low_fn1)
    2'b00: dout = byte_adj_out;
    2'b01: dout = word_adj_out;
    2'b10: dout = reg_bout;
    2'b11: dout = 0;
    endcase
end

endmodule

//FIX PROBLEM WITH MEMORY LOAD ACCESS DIN, WRONG LDW ADDR, EMPTY LDD ADDR

//0. C_WE
//1. ALU_Bsel
//2. PC_JMP
//3. SR_WE
//4. MEM_WE
//5. KS
//6-8. PC_IN: JMP, COND_JMP, IJR, DB_In, IRD
//9-10. REG_IN: ALU, UPPER_IMM, MEM
//11-12. MEM_ADDR: Store, Load, S_INT, H_INT
//13. IR_tsf
//14. Mem_REQ
*/

/* Code of regfile:
module regfile(
    input [31:0] din,
    input clk,
    input c_we,
    input ir_tsf,
    input sr_in,
    input sr_we,
    input ks,
    input [1:0] sr_sel,
    input [4:0] asel,
    input [4:0] bsel,
    input [4:0] csel,
    input [31:0] pc,
    output reg [31:0] aout,
    output reg [31:0] bout,
    output [31:0] ir,
    output [3:0] sr
);

reg [3:0] status = 4'b1000;
reg [31:0] memory [31:0];
always_ff @(posedge clk) begin
    if(c_we) begin
        memory[csel] <= din;
    end
    if(ir_tsf) begin
        memory[5'h1d] <= pc;
    end
end

always_ff @(posedge clk) begin
    if(sr_we && status[0]) begin
        status[sr_sel] <= sr_in;
    end
    if(ks) begin
        status[0] = 1;
    end
end

always_comb begin
    case(asel)
    5'h0: aout = 0;
    5'h1: aout = status;
    5'h2: aout = pc;
    default: aout = memory[asel];
    endcase
    case(bsel)
    5'h0: bout = 0;
    5'h1: bout = status;
    5'h2: bout = pc;
    default: bout = memory[bsel];
    endcase
end

assign ir = memory[5'h3];
assign sr = memory[5'h1];

endmodule
*/

/* Code of ProgramCounter:
module ProgramCounter(
    input wire [31:0] din,
    input wire we,
    input wire clk,
    input wire jmp,
    input wire rst,
    output wire [31:0] dout
    
);

reg [31:0] pc = 8;
always_ff @(posedge clk) begin
    if(we) begin
        if(!jmp && !rst) begin
            pc <= pc + 4;
        end
        if(jmp && !rst) begin
            pc <= din;
        end
        if(rst) begin
            pc <= 0;
        end
    end
end

assign dout = pc;

endmodule
*/

/* Code of alu:
module alu(
    input [31:0] a,
    input [31:0] b,
    input [3:0] op,
    output logic [31:0] res,
    output [3:0] sub_flags
);

always_comb begin
    case(op)
    4'h0: res = final_addition;
    4'h1: res = final_subtraction;
    4'h2: res = a & b;
    4'h3: res = a | b;
    4'h4: res = a ^ b;
    4'h5: res = a >> b;
    4'h6: res = a >>> b;
    4'h7: res = a << b;
    4'h8: res = {31'h0, add_carry};
    4'h9: res = {31'h0, sub_borrow};
    default: res = 0;
    endcase
end

wire [32:0] intermediate_addition = {1'b0, a} + {1'b0, b};
wire [32:0] intermediate_subtraction = {1'b0, a} - {1'b0, b};
wire sub_borrow = intermediate_subtraction[32];
wire add_carry = intermediate_addition[32];
wire [31:0] final_addition = intermediate_addition[31:0];
wire [31:0] final_subtraction = intermediate_subtraction[31:0];

assign sub_flags = {((a[31] == b[31]) && (final_subtraction[31] != a[31])), intermediate_subtraction[31], sub_borrow, {!(|(a - b))}}; //zero, borrow, sign, overflow

endmodule : alu
*/
